# Fritzing sketch MidiModule-V2 (saved by Fritzing 1.0.7)
circuit board: 3.96305cm x 2.20169cm
breadboards: 1

parts:
  d_-_+ = male pin header, 3 pins [form="♂ (male)"]
  IC = H11AA1 [part_number=H11L1 package=dil06]
  D1 = Rectifier Diode [part_number=1N4148 package="300 mil [THT]"]
  MIDI_In = DIN-5 jack (MIDI) [package=THT]
  R1 = Resistor [tolerance=±5% resistance=220 power=0.25 package="1206 [SMD]"]
  R2 = Resistor [tolerance=±5% resistance=470 power=0.25 package="1206 [SMD]"]
  C1 = Ceramic Capacitor [capacitance=100nF voltage=35V package="0805 [SMD, multilayer]"]

nets:
  N1: d_-_+.pin1, IC.B, R2.Pin_0, C1.0
  N2: d_-_+.pin2, IC.C, C1.1
  N3: d_-_+.pin3, IC.E, R2.Pin_1
  N4: IC.A/C, D1.cathode, R1.Pin_0
  N5: IC.C/A, D1.anode, MIDI_In.5
  N6: MIDI_In.4, R1.Pin_1

notes:
  MidiModule v2

custom parts:
  H11AA1: The H11AA1 is a bi-directional input optically coupled isolator consisting of two inverse parallel gallium arsenide infrared LEDs coupled to a silicon NPN phototransistor in a 6 pin DIP package.
  DIN-5 jack (MIDI): Female DIN connector with 5 pins, as used for MIDI and SYNC
