# Fritzing sketch MidiModule (saved by Fritzing 1.0.1rc)
circuit board: 3.41341cm x 1.73521cm
breadboards: 1

parts:
  R1 = Resistor [tolerance=±5% power=0.25 resistance=220 package=THT]
  R2 = Resistor [tolerance=±5% power=0.25 resistance=470 package=THT]
  d_-_+ = male pin header, 3 pins [form="♂ (male)"]
  IC = H11AA1 [part_number=H11L1 package=dil06]
  MIDI_IN = DIN-5 jack (MIDI) [package=THT]
  D1 = Rectifier Diode [part_number=1N4148 package="300 mil [THT]"]
  C1 = Ceramic Capacitor [capacitance=100nF voltage=35V package="200 mil [THT, multilayer]"]

nets:
  N1: R1.Pin_0, IC.A/C, D1.cathode
  N2: R1.Pin_1, MIDI_IN.4
  N3: R2.Pin_0, d_-_+.pin1, IC.B, C1.0
  N4: R2.Pin_1, d_-_+.pin3, IC.E
  N5: d_-_+.pin2, IC.C, C1.1
  N6: IC.C/A, MIDI_IN.5, D1.anode

custom parts:
  H11AA1: The H11AA1 is a bi-directional input optically coupled isolator consisting of two inverse parallel gallium arsenide infrared LEDs coupled to a silicon NPN phototransistor in a 6 pin DIP package.
